# Fritzing sketch RestroomEntry (saved by Fritzing 0.9.3b)
breadboards: 2

parts:
  Componente1 = Arduino Mega 2560 (Rev3)
  J1 = Basic Force Sensing Resistor (FSR) [package=THT]
  HC-SR04_Sensor_1 = HC-SR04 Ultrasonic Distance Sensor
  Componente5 = Gas Sensor Breakout Board
  R2 = Resistor [tolerance=±5% resistance=22k package=THT]

nets:
  N1: Componente1.A0, Componente5.B2, Componente5.B1, R2.Pin_0
  N2: Componente1.A1, J1.pin_1
  5V: Componente1.5V, J1.pin_0, HC-SR04_Sensor_1.VCC, Componente5.A1, Componente5.A2, Componente5.H1
  GND: Componente1.GND, HC-SR04_Sensor_1.GND, Componente5.GND, R2.Pin_1
  N3: Componente1.D2_PWM, HC-SR04_Sensor_1.ECHO
  N4: Componente1.D3_PWM, HC-SR04_Sensor_1.TRIG

notes:
  DC IN:
  7V
  Force resistor
  Ultrasonic sensor
  MQ-7 Sensor Breakout
  Sink module (1 module for sink)
  1) UltraSonic for garbage level
  2) Force resistor for soap level
  It needs 5 pins
  VCC - 5V
  GND - GND
  A0 - Resistor Out
  D0 - US echo
  D1 - US trigger
  Restroom entrance module
  (1 module for restroom)
  It needs 3 pins
  VCC - 5V
  GND - GND
  A0 - Smoke out
