# Fritzing sketch RestroomSM (saved by Fritzing 0.9.3b)
breadboards: 5

parts:
  Componente1 = Arduino Mega 2560 (Rev3)
  Power_plug1 = Power plug
  Componente2 = HC-SR501 Body Sensor Module
  S1 = SWITCH-MOMENTARY-2 [package=reed_switch_pth]
  IR1 = TSOP312.., 314.. [package=THT]
  Grove1 = Grove Infrared Emitter
  R1 = Resistor [tolerance=±5% resistance=330 package="2010 [SMD]"]
  Q1 = MOSFET-NCHANNEL [package=to-92]
  Water_Level_Sensor1 = Water Level Sensor
  Componente3 = HC-SR501 Body Sensor Module
  S2 = SWITCH-MOMENTARY-2 [package=reed_switch_pth]
  IR2 = TSOP312.., 314.. [package=THT]
  Grove2 = Grove Infrared Emitter
  Q2 = MOSFET-NCHANNEL [package=to-92]
  Water_Level_Sensor2 = Water Level Sensor
  Componente4 = HC-SR501 Body Sensor Module
  S3 = SWITCH-MOMENTARY-2 [package=reed_switch_pth]
  IR3 = TSOP312.., 314.. [package=THT]
  Grove3 = Grove Infrared Emitter
  Q3 = MOSFET-NCHANNEL [package=to-92]
  Water_Level_Sensor3 = Water Level Sensor
  J1 = Basic Force Sensing Resistor (FSR) [package=THT]
  HC-SR04_Sensor_1 = HC-SR04 Ultrasonic Distance Sensor
  J2 = Basic Force Sensing Resistor (FSR) [package=THT]
  HC-SR04_Sensor_2 = HC-SR04 Ultrasonic Distance Sensor
  J3 = Basic Force Sensing Resistor (FSR) [package=THT]
  HC-SR04_Sensor_3 = HC-SR04 Ultrasonic Distance Sensor
  Componente5 = Gas Sensor Breakout Board
  R2 = Resistor [tolerance=±5% resistance=220 package=THT]

nets:
  N1: Componente1.A0, Water_Level_Sensor3.SIG
  N2: Componente1.A1, Water_Level_Sensor2.SIG
  N3: Componente1.A2, Water_Level_Sensor1.SIG
  N4: Componente1.A3, J3.pin_1
  N5: Componente1.A4, J2.pin_1
  N6: Componente1.A5, J1.pin_1
  N7: Componente1.A6, Componente5.B2, Componente5.B1, R2.Pin_0
  N8: Componente1.D10_PWM, HC-SR04_Sensor_3.TRIG
  N9: Componente1.D9_PWM, HC-SR04_Sensor_2.TRIG
  N10: Componente1.D8_PWM, HC-SR04_Sensor_1.TRIG
  GND: Componente1.GND, Power_plug1.GND, Componente2.GND, IR1.GND, Grove1.GND, Water_Level_Sensor1.GND, Componente3.GND, IR2.GND, Grove2.GND, Water_Level_Sensor2.GND, Componente4.GND, IR3.GND, Grove3.GND, Water_Level_Sensor3.GND, HC-SR04_Sensor_1.GND, HC-SR04_Sensor_2.GND, HC-SR04_Sensor_3.GND, Componente5.GND, R2.Pin_1
  VIN: Componente1.VIN, Power_plug1.VCC, R1.Pin_0
  N11: Componente1.D2_PWM, Grove1.TX
  N12: Componente1.D3_PWM, Grove2.TX
  N13: Componente1.D4_PWM, Grove3.TX
  N14: Componente1.D5_PWM, Q1.G
  N15: Componente1.D6_PWM, Q2.G
  N16: Componente1.D7_PWM, Q3.G
  N17: Componente1.D22, Componente2.OUT
  N18: Componente1.D23, Componente3.OUT
  N19: Componente1.D24, Componente4.OUT
  N20: Componente1.D28, S1.2
  N21: Componente1.D29, S2.2
  N22: Componente1.D30, S3.2
  N23: Componente1.D31, IR1.Data
  N24: Componente1.D32, IR2.Data
  N25: Componente1.D33, IR3.Data
  N26: Componente1.D40, HC-SR04_Sensor_1.ECHO
  N27: Componente1.D41, HC-SR04_Sensor_2.ECHO
  N28: Componente1.D42, HC-SR04_Sensor_3.ECHO
  VCC: Componente2.VCC, S1.1, IR1.Vs, Grove1.VCC, R1.Pin_1, Water_Level_Sensor1.VCC, Componente3.VCC, S2.1, IR2.Vs, Grove2.VCC, Water_Level_Sensor2.VCC, Componente4.VCC, S3.1, IR3.Vs, Grove3.VCC, Water_Level_Sensor3.VCC, J1.pin_0, HC-SR04_Sensor_1.VCC, J2.pin_0, HC-SR04_Sensor_2.VCC, J3.pin_0, HC-SR04_Sensor_3.VCC, Componente5.A2, Componente5.H1, Componente5.A1

notes:
  MOTION SENSOR
  REED SWITCH
  IR RECEIVER
  PNP POWER TRANSISTOR
  WATER LEVER SENSOR
  IR EMITTER
  DC IN:
  7V
  Force resistor
  Ultrasonic sensor
  MQ-7 Sensor Breakout

custom parts:
  HC-SR501 Body Sensor Module: Pyroelectric Infrared PIR Motion Sensor Detector Module
  Water Level Sensor: A water level sensor. This sensor operates at 3V to 5V. The Sig (signal) pin outputs an analogue signal that is in proportion to the amount of water in contact with the sensor.
