# Fritzing sketch RestroomCell (saved by Fritzing 0.9.3b)
breadboards: 1

parts:
  Componente1 = Arduino Mega 2560 (Rev3)
  R1 = PHOTOCELL [package=photocell-kit]
  RHT1 = Humidity and Temperature Sensor RHT03
  KY-008_Laserdiode1 = Laser [part_number=1219301 package=keys]
  KY-008_Laserdiode2 = Laser [part_number=1219301 package=keys]
  R2 = PHOTOCELL [package=photocell-kit]
  R3 = PHOTOCELL [package=photocell-kit]

nets:
  N1: Componente1.A1, R1.P$1
  N2: Componente1.A2, R3.P$1
  N3: Componente1.A3, R2.P$1
  5V: Componente1.5V, R1.P$2, RHT1.Vcc, KY-008_Laserdiode1.connector1pin, KY-008_Laserdiode2.connector1pin, R2.P$2, R3.P$2
  N4: Componente1.GND, RHT1.GND_1, KY-008_Laserdiode1.connector2pin, KY-008_Laserdiode2.connector2pin
  N5: Componente1.D2_PWM, KY-008_Laserdiode1.connector0pin
  N6: Componente1.D3_PWM, KY-008_Laserdiode2.connector0pin
  N7: Componente1.D4_PWM, RHT1.Data-signal

notes:
  LASER
  DIODE
  -
  DOOR
  CLOSED
  CHECK
  Photoresistor
  -
  LIGHT
  CHECK
  temp
  and
  humidity
  -
  HUMIDITY CHECK
  LASER
  DIODE
  -
  PAPER
  AVAILABLE
  CHECK
  Photoresistor
  -
  PAPER AVAILABLE CHECK
  Photoresistor
  -
  DOOR
  CLOSED
  CHECK
  7V DC
  USB PORT CONNECTED TO RASPBERRY
  Bathroom cell module
  (1module per cell)
  It needs 8 pins to work
  VCC - 5V
  GND - GND
  D0 - Door Laser diode In
  D1 - Paper Laser diode In
  D2 - Humidity sensor out
  A0 - Door photoresistor out
  A1 - Paper photoresistor out
  A2 - Light photoresistor out

custom parts:
  Laser: KEYES KY-008 650nm Laser Transmitter Module
